// Logisim project TESTE.circ as structural Verilog: 2 circuits, main circuit main
module main (
);

  wire A_q, and_1_out, B_q, bin_7_segmentos_1_a, bin_7_segmentos_1_b, bin_7_segmentos_1_c,
       bin_7_segmentos_1_d, bin_7_segmentos_1_e, bin_7_segmentos_1_f, bin_7_segmentos_1_g, C_q, clock_1_out,
       D_q, D_qn;

  Clock clock_1 (.out(clock_1_out));
  J_K_Flip_Flop A (.J(D_q), .clk(clock_1_out), .K(B_q), .Q(A_q));  // open: Qn, preset, en, reset
  J_K_Flip_Flop B (.J(1'b1), .clk(clock_1_out), .K(1'b1), .Q(B_q));  // open: Qn, preset, en, reset
  BIN___7_SEGMENTOS bin_7_segmentos_1 (
    .BIT3(A_q), .BIT2(B_q), .BIT1(C_q), .BIT0(D_q), .A(bin_7_segmentos_1_a), .B(bin_7_segmentos_1_b),
    .C(bin_7_segmentos_1_c), .D(bin_7_segmentos_1_d), .E(bin_7_segmentos_1_e), .F(bin_7_segmentos_1_f),
    .G(bin_7_segmentos_1_g));
  J_K_Flip_Flop C (.J(and_1_out), .clk(clock_1_out), .K(1'b1), .Q(C_q));  // open: Qn, preset, en, reset
  and and_1 (and_1_out, B_q, D_qn);
  _7_Segment_Display u_7_segment_display_1 (
    .g(bin_7_segmentos_1_a), .f(bin_7_segmentos_1_b), .a(bin_7_segmentos_1_c), .b(bin_7_segmentos_1_d),
    .e(bin_7_segmentos_1_g), .d(bin_7_segmentos_1_f), .c(bin_7_segmentos_1_e));  // open: dp
  J_K_Flip_Flop D (.J(C_q), .clk(clock_1_out), .K(1'b1), .Q(D_q), .Qn(D_qn));  // open: preset, en, reset
endmodule

module BIN___7_SEGMENTOS (
  input  BIT3,
  input  BIT2,
  input  BIT1,
  input  BIT0,
  output A,
  output B,
  output C,
  output D,
  output E,
  output F,
  output G
);

  wire and_1_out, not_1_out, not_2_out, not_5_out, not_6_out;

  not not_1 (not_1_out, BIT3);
  or or_1 (A, not_1_out, not_2_out);
  not not_2 (not_2_out, BIT2);
  not not_3 (B, BIT1);
  not not_4 (D, BIT2);
  not not_5 (not_5_out, BIT2);
  and and_1 (and_1_out, not_5_out, not_6_out);
  not not_6 (not_6_out, BIT1);
  not not_7 (G, BIT0);
  or or_2 (E, and_1_out, BIT0);

  assign C = 1'b1;
  assign F = 1'b1;
endmodule
