// Logisim project binário - decimal.circ as structural Verilog: 1 circuit, main circuit main
module main (
  input  BIT3,
  input  BIT2,
  input  BIT1,
  input  BIT0,
  output _0,
  output _1,
  output _2,
  output _3,
  output _4,
  output _5,
  output _6,
  output _7,
  output _8,
  output _9
);

  and and_1 (_0, ~BIT3, ~BIT2, ~BIT1, ~BIT0);  // AND_Gate
  and and_2 (_1, ~BIT3, ~BIT2, ~BIT1, BIT0);  // AND_Gate
  and and_3 (_2, ~BIT2, BIT1, ~BIT0);  // AND_Gate
  and and_4 (_3, ~BIT2, BIT1, BIT0);  // AND_Gate
  and and_5 (_4, BIT2, ~BIT1, ~BIT0);  // AND_Gate
  and and_6 (_5, BIT2, ~BIT1, BIT0);  // AND_Gate
  and and_7 (_6, BIT2, BIT1, ~BIT0);  // AND_Gate
  and and_8 (_7, BIT2, BIT1, BIT0);
  and and_9 (_8, BIT3, ~BIT0);  // AND_Gate
  and and_10 (_9, BIT3, BIT0);
endmodule
