// Logisim project contador 0a3 crescente e decrescente.circ as structural Verilog: 3 circuits, main circuit main
module main (
  input  in_1
);

  wire clock_1_out, j_k_ff_1_qn;
  wire [1:0] demultiplexer_1_out0, demultiplexer_1_out1, j_k_ff_1_q;
  wire [6:0] bin_7seg_0_3_1_a, bin_7seg_3_0_1_a, multiplexer_1_out;

  Clock clock_1 (.out(clock_1_out));
  J_K_Flip_Flop j_k_ff_1 (
    .J(1'b1), .clk(clock_1_out), .K(1'b1), .Q(j_k_ff_1_q[0]), .Qn(j_k_ff_1_qn));  // open: preset, en, reset
  J_K_Flip_Flop j_k_ff_2 (.J(1'b1), .clk(j_k_ff_1_qn), .K(1'b1), .Q(j_k_ff_1_q[1]));  // open: Qn, preset, en, reset
  Demultiplexer #(.width(2)) demultiplexer_1 (
    .out0(demultiplexer_1_out0), .out1(demultiplexer_1_out1), .in(j_k_ff_1_q), .sel(in_1));  // open: en
  bin_7seg___0_3 bin_7seg_0_3_1 (
    .bit1(demultiplexer_1_out0[1]), .bit0(demultiplexer_1_out0[0]), .a(bin_7seg_0_3_1_a[0]),
    .b(bin_7seg_0_3_1_a[1]), .c(bin_7seg_0_3_1_a[2]), .d(bin_7seg_0_3_1_a[3]), .e(bin_7seg_0_3_1_a[4]),
    .f(bin_7seg_0_3_1_a[5]), .g(bin_7seg_0_3_1_a[6]));
  bin_7seg___3_0 bin_7seg_3_0_1 (
    .bit1(demultiplexer_1_out1[1]), .bit0(demultiplexer_1_out1[0]), .a(bin_7seg_3_0_1_a[0]),
    .b(bin_7seg_3_0_1_a[1]), .c(bin_7seg_3_0_1_a[2]), .d(bin_7seg_3_0_1_a[3]), .e(bin_7seg_3_0_1_a[4]),
    .f(bin_7seg_3_0_1_a[5]), .g(bin_7seg_3_0_1_a[6]));
  Multiplexer #(.width(7)) multiplexer_1 (
    .in0(bin_7seg_0_3_1_a), .in1(bin_7seg_3_0_1_a), .out(multiplexer_1_out), .sel(in_1));  // open: en
  _7_Segment_Display u_7_segment_display_1 (
    .g(multiplexer_1_out[0]), .f(multiplexer_1_out[1]), .a(multiplexer_1_out[2]), .b(multiplexer_1_out[3]),
    .e(multiplexer_1_out[6]), .d(multiplexer_1_out[5]), .c(multiplexer_1_out[4]));  // open: dp
endmodule

module bin_7seg___0_3 (
  input  bit1,
  input  bit0,
  output a,
  output b,
  output c,
  output d,
  output e,
  output f,
  output g
);

  wire not_1_out, not_2_out, not_3_out, not_4_out, not_5_out;

  not not_1 (not_1_out, bit1);
  not not_2 (not_2_out, bit0);
  not not_3 (not_3_out, bit0);
  not not_4 (not_4_out, bit1);
  not not_5 (not_5_out, bit0);
  not not_6 (g, bit0);
  and and_1 (b, not_1_out, not_2_out);
  or or_1 (c, not_3_out, bit1);
  or or_2 (e, not_4_out, bit0);
  or or_3 (f, not_5_out, bit1);

  assign a = bit1;
  assign d = 1'b1;
endmodule

module bin_7seg___3_0 (
  input  bit1,
  input  bit0,
  output a,
  output b,
  output c,
  output d,
  output e,
  output f,
  output g
);

  wire not_2_out, not_3_out, not_4_out;

  not not_1 (a, bit1);
  and and_1 (b, bit1, bit0);
  not not_2 (not_2_out, bit1);
  not not_3 (not_3_out, bit0);
  not not_4 (not_4_out, bit1);
  or or_1 (c, not_2_out, bit0);
  or or_2 (e, not_3_out, bit1);
  or or_3 (f, not_4_out, bit0);

  assign d = 1'b1;
  assign g = bit0;
endmodule
