// Logisim project contador segundos.circ as structural Verilog: 4 circuits, main circuit main
module main (
);

  wire binario_7seg_1_a, binario_7seg_1_b, binario_7seg_1_c, binario_7seg_1_d, binario_7seg_1_e,
       binario_7seg_1_f, binario_7seg_1_g, binario_7seg_2_a, binario_7seg_2_b, binario_7seg_2_c,
       binario_7seg_2_d, binario_7seg_2_e, binario_7seg_2_f, binario_7seg_2_g, clock_1_out,
       contador_0_5_1_bit0, contador_0_5_1_bit1, contador_0_5_1_bit3, contador_0_9_1_bit0,
       contador_0_9_1_bit1, contador_0_9_1_bit2, contador_0_9_1_bit3, contador_0_9_1_clock_saida;

  contador_0_5 contador_0_5_1 (
    .clock(contador_0_9_1_clock_saida), .bit0(contador_0_5_1_bit0), .bit1(contador_0_5_1_bit1),
    .bit3(contador_0_5_1_bit3));
  binario_7seg binario_7seg_1 (
    .bit3(1'b0), .bit2(contador_0_5_1_bit3), .bit1(contador_0_5_1_bit1), .bit0(contador_0_5_1_bit0),
    .a(binario_7seg_1_a), .b(binario_7seg_1_b), .c(binario_7seg_1_c), .d(binario_7seg_1_d),
    .e(binario_7seg_1_e), .f(binario_7seg_1_f), .g(binario_7seg_1_g));
  Clock clock_1 (.out(clock_1_out));
  contador_0_9 contador_0_9_1 (
    .Clock_Saida(contador_0_9_1_clock_saida), .CLOCK(clock_1_out), .BIT0(contador_0_9_1_bit0),
    .bit1(contador_0_9_1_bit1), .bit2(contador_0_9_1_bit2), .bit3(contador_0_9_1_bit3));
  _7_Segment_Display u_7_segment_display_1 (
    .g(binario_7seg_1_a), .f(binario_7seg_1_b), .a(binario_7seg_1_c), .b(binario_7seg_1_d),
    .e(binario_7seg_1_g), .d(binario_7seg_1_f), .c(binario_7seg_1_e));  // open: dp
  binario_7seg binario_7seg_2 (
    .bit3(contador_0_9_1_bit3), .bit2(contador_0_9_1_bit2), .bit1(contador_0_9_1_bit1),
    .bit0(contador_0_9_1_bit0), .a(binario_7seg_2_a), .b(binario_7seg_2_b), .c(binario_7seg_2_c),
    .d(binario_7seg_2_d), .e(binario_7seg_2_e), .f(binario_7seg_2_f), .g(binario_7seg_2_g));
  _7_Segment_Display u_7_segment_display_2 (
    .g(binario_7seg_2_a), .f(binario_7seg_2_b), .a(binario_7seg_2_c), .b(binario_7seg_2_d),
    .e(binario_7seg_2_g), .d(binario_7seg_2_f), .c(binario_7seg_2_e));  // open: dp
endmodule

module binario_7seg (
  input  bit3,
  input  bit2,
  input  bit1,
  input  bit0,
  output a,
  output b,
  output c,
  output d,
  output e,
  output f,
  output g
);

  wire and_1_out, and_2_out, and_3_out, and_4_out, and_5_out, and_6_out, and_7_out, and_8_out, and_9_out,
       and_10_out, and_11_out, and_12_out, and_13_out, and_14_out, and_15_out, and_16_out, not_1_out,
       not_2_out, not_3_out, not_4_out, not_5_out, not_6_out, not_7_out, not_8_out, not_9_out, not_10_out,
       not_11_out, not_12_out, not_13_out, not_14_out, not_15_out, not_16_out, not_17_out, not_18_out,
       not_19_out, not_20_out, not_21_out;

  not not_1 (not_1_out, bit2);
  and and_1 (and_1_out, not_1_out, bit1);
  and and_2 (and_2_out, bit2, not_2_out);
  not not_2 (not_2_out, bit1);
  and and_3 (and_3_out, bit2, not_3_out);
  not not_3 (not_3_out, bit0);
  not not_4 (not_4_out, bit1);
  and and_4 (and_4_out, not_4_out, not_5_out);
  not not_5 (not_5_out, bit0);
  and and_5 (and_5_out, bit2, not_6_out);
  not not_6 (not_6_out, bit1);
  and and_6 (and_6_out, bit2, not_7_out);
  not not_7 (not_7_out, bit0);
  not not_8 (not_8_out, bit2);
  and and_7 (and_7_out, not_8_out, not_9_out);
  not not_9 (not_9_out, bit0);
  and and_8 (and_8_out, bit2, bit0);
  not not_10 (not_10_out, bit2);
  not not_11 (not_11_out, bit1);
  and and_9 (and_9_out, not_11_out, not_12_out);
  not not_12 (not_12_out, bit0);
  and and_10 (and_10_out, bit1, bit0);
  not not_13 (not_13_out, bit1);
  or or_1 (e, not_13_out, bit0, bit2);
  not not_14 (not_14_out, bit2);
  and and_11 (and_11_out, not_14_out, not_15_out);
  not not_15 (not_15_out, bit0);
  not not_16 (not_16_out, bit2);
  and and_12 (and_12_out, not_16_out, bit1);
  and and_13 (and_13_out, bit1, not_17_out);
  not not_17 (not_17_out, bit0);
  and and_14 (and_14_out, bit2, not_18_out, bit0);
  not not_18 (not_18_out, bit1);
  not not_19 (not_19_out, bit2);
  and and_15 (and_15_out, not_19_out, not_20_out);
  not not_20 (not_20_out, bit0);
  and and_16 (and_16_out, bit1, not_21_out);
  not not_21 (not_21_out, bit0);
  or or_2 (a, and_1_out, and_2_out, and_3_out, bit3);
  or or_3 (b, and_4_out, and_5_out, and_6_out, bit3);
  or or_4 (c, and_7_out, bit1, and_8_out, bit3);
  or or_5 (d, not_10_out, and_9_out, and_10_out);
  or or_6 (f, and_11_out, and_12_out, and_13_out, and_14_out, bit3);
  or or_7 (g, and_15_out, and_16_out);
endmodule

module contador_0_9 (
  input  CLOCK,
  output Clock_Saida,
  output BIT0,
  output bit1,
  output bit2,
  output bit3
);

  wire j_k_ff_1_qn, j_k_ff_2_qn, j_k_ff_3_qn;

  and and_1 (Clock_Saida, bit3, bit1);
  J_K_Flip_Flop j_k_ff_1 (
    .J(1'b1), .clk(CLOCK), .K(1'b1), .Q(BIT0), .Qn(j_k_ff_1_qn), .reset(Clock_Saida));  // open: preset, en
  J_K_Flip_Flop j_k_ff_2 (
    .J(1'b1), .clk(j_k_ff_1_qn), .K(1'b1), .Q(bit1), .Qn(j_k_ff_2_qn), .reset(Clock_Saida));  // open: preset, en
  J_K_Flip_Flop j_k_ff_3 (
    .J(1'b1), .clk(j_k_ff_2_qn), .K(1'b1), .Q(bit2), .Qn(j_k_ff_3_qn), .reset(Clock_Saida));  // open: preset, en
  J_K_Flip_Flop j_k_ff_4 (
    .J(1'b1), .clk(j_k_ff_3_qn), .K(1'b1), .Q(bit3), .reset(Clock_Saida));  // open: Qn, preset, en
endmodule

module contador_0_5 (
  input  clock,
  output bit0,
  output bit1,
  output bit3
);

  wire and_1_out, j_k_ff_1_qn, j_k_ff_2_qn;

  and and_1 (and_1_out, bit3, bit1);
  J_K_Flip_Flop j_k_ff_1 (
    .J(1'b1), .clk(clock), .K(1'b1), .Q(bit0), .Qn(j_k_ff_1_qn), .reset(and_1_out));  // open: preset, en
  J_K_Flip_Flop j_k_ff_2 (
    .J(1'b1), .clk(j_k_ff_1_qn), .K(1'b1), .Q(bit1), .Qn(j_k_ff_2_qn), .reset(and_1_out));  // open: preset, en
  J_K_Flip_Flop j_k_ff_3 (.J(1'b1), .clk(j_k_ff_2_qn), .K(1'b1), .Q(bit3), .reset(and_1_out));  // open: Qn, preset, en
endmodule
