// Logisim project decimal - 7seg = binario - 7seg = gray - 7seg.circ as structural Verilog: 5 circuits, main circuit main
module main (
);

  wire _0_out, _1_out, _2_out, _3_out, _4_out, _5_out, _6_out, _7_out, _8_out, _9_out,
       binario_7_segmentos_1_a, binario_7_segmentos_1_a_2, binario_7_segmentos_1_a_3,
       binario_7_segmentos_1_a_4, binario_7_segmentos_1_b, binario_7_segmentos_1_b_2,
       binario_7_segmentos_1_b_3, binario_7_segmentos_1_b_4, binario_7_segmentos_1_c,
       binario_7_segmentos_1_c_2, binario_7_segmentos_1_c_3, binario_7_segmentos_1_c_4,
       binario_7_segmentos_1_d, binario_7_segmentos_1_d_2, binario_7_segmentos_1_d_3,
       binario_7_segmentos_1_d_4, binario_7_segmentos_1_e, binario_7_segmentos_1_e_2,
       binario_7_segmentos_1_e_3, binario_7_segmentos_1_e_4, binario_7_segmentos_1_f,
       binario_7_segmentos_1_f_2, binario_7_segmentos_1_f_3, binario_7_segmentos_1_f_4,
       binario_7_segmentos_1_g, binario_7_segmentos_1_g_2, binario_7_segmentos_1_g_3,
       binario_7_segmentos_1_g_4, binario_7_segmentos_2_a, binario_7_segmentos_2_a_2,
       binario_7_segmentos_2_a_3, binario_7_segmentos_2_a_4, binario_7_segmentos_2_b,
       binario_7_segmentos_2_b_2, binario_7_segmentos_2_b_3, binario_7_segmentos_2_b_4,
       binario_7_segmentos_2_c, binario_7_segmentos_2_c_2, binario_7_segmentos_2_c_3,
       binario_7_segmentos_2_c_4, binario_7_segmentos_2_d, binario_7_segmentos_2_d_2,
       binario_7_segmentos_2_d_3, binario_7_segmentos_2_d_4, binario_7_segmentos_2_e,
       binario_7_segmentos_2_e_2, binario_7_segmentos_2_e_3, binario_7_segmentos_2_e_4,
       binario_7_segmentos_2_f, binario_7_segmentos_2_f_2, binario_7_segmentos_2_f_3,
       binario_7_segmentos_2_f_4, binario_7_segmentos_2_g, binario_7_segmentos_2_g_2,
       binario_7_segmentos_2_g_3, binario_7_segmentos_2_g_4, \binário_gray_1_bit0_2 ,
       \binário_gray_1_bit1_2 , \binário_gray_1_bit2_2 , \binário_gray_1_bit3_2 , \decimal_binário_1_bit0 ,
       \decimal_binário_1_bit1 , \decimal_binário_1_bit2 , \decimal_binário_1_bit3 , n7_segmentos_1_a,
       n7_segmentos_1_b, n7_segmentos_1_c, n7_segmentos_1_d, n7_segmentos_1_e, n7_segmentos_1_f,
       n7_segmentos_1_g;

  Button _0 (.out(_0_out));
  Button _1 (.out(_1_out));
  Button _3 (.out(_3_out));
  Button _2 (.out(_2_out));
  Button _4 (.out(_4_out));
  Button _6 (.out(_6_out));
  Button _5 (.out(_5_out));
  \DECIMAL___BINÁRIO  \decimal_binário_1  (
    ._0(_0_out), ._1(_1_out), ._2(_2_out), ._3(_3_out), ._4(_4_out), ._5(_5_out), ._6(_6_out), ._7(_7_out),
    ._8(_8_out), ._9(_9_out), .bit3(\decimal_binário_1_bit3 ), .bit2(\decimal_binário_1_bit2 ),
    .bit1(\decimal_binário_1_bit1 ), .bit0(\decimal_binário_1_bit0 ));
  BINARIO___7_SEGMENTOS binario_7_segmentos_1 (
    .Bit3(\decimal_binário_1_bit3 ), .Bit2(\decimal_binário_1_bit2 ), .Bit1(\decimal_binário_1_bit1 ),
    .Bit0(\decimal_binário_1_bit0 ), .A(binario_7_segmentos_1_a), .B(binario_7_segmentos_1_b),
    .C(binario_7_segmentos_1_c), .D(binario_7_segmentos_1_d), .E(binario_7_segmentos_1_e),
    .F(binario_7_segmentos_1_f), .G(binario_7_segmentos_1_g), .A_2(binario_7_segmentos_1_a_2),
    .B_2(binario_7_segmentos_1_b_2), .C_2(binario_7_segmentos_1_c_2), .D_2(binario_7_segmentos_1_d_2),
    .E_2(binario_7_segmentos_1_e_2), .F_2(binario_7_segmentos_1_f_2), .G_2(binario_7_segmentos_1_g_2),
    .A_3(binario_7_segmentos_1_a_3), .B_3(binario_7_segmentos_1_b_3), .C_3(binario_7_segmentos_1_c_3),
    .D_3(binario_7_segmentos_1_d_3), .E_3(binario_7_segmentos_1_e_3), .F_3(binario_7_segmentos_1_f_3),
    .G_3(binario_7_segmentos_1_g_3), .A_4(binario_7_segmentos_1_a_4), .B_4(binario_7_segmentos_1_b_4),
    .C_4(binario_7_segmentos_1_c_4), .D_4(binario_7_segmentos_1_d_4), .E_4(binario_7_segmentos_1_e_4),
    .F_4(binario_7_segmentos_1_f_4), .G_4(binario_7_segmentos_1_g_4));
  Button _8 (.out(_8_out));
  Button _9 (.out(_9_out));
  Button _7 (.out(_7_out));
  _7_segmentos u_7_segmentos_1 (
    .bit_3(\decimal_binário_1_bit3 ), .bit_2(\decimal_binário_1_bit2 ), .bit_1(\decimal_binário_1_bit1 ),
    .bit_0(\decimal_binário_1_bit0 ), .A(n7_segmentos_1_a), .B(n7_segmentos_1_b), .C(n7_segmentos_1_c),
    .D(n7_segmentos_1_d), .E(n7_segmentos_1_e), .F(n7_segmentos_1_f), .G(n7_segmentos_1_g));
  _7_Segment_Display u_7_segment_display_1 (
    .g(binario_7_segmentos_1_g_3), .f(binario_7_segmentos_1_f_3), .a(binario_7_segmentos_1_a_3),
    .b(binario_7_segmentos_1_b_3), .e(binario_7_segmentos_1_e_3), .d(binario_7_segmentos_1_d_3),
    .c(binario_7_segmentos_1_c_3));  // open: dp
  _7_Segment_Display u_7_segment_display_2 (
    .g(binario_7_segmentos_1_g_4), .f(binario_7_segmentos_1_f_4), .a(binario_7_segmentos_1_a_4),
    .b(binario_7_segmentos_1_b_4), .e(binario_7_segmentos_1_e_4), .d(binario_7_segmentos_1_d_4),
    .c(binario_7_segmentos_1_c_4));  // open: dp
  _7_Segment_Display u_7_segment_display_3 (
    .g(n7_segmentos_1_g), .f(n7_segmentos_1_f), .a(n7_segmentos_1_a), .b(n7_segmentos_1_b),
    .e(n7_segmentos_1_e), .d(n7_segmentos_1_d), .c(n7_segmentos_1_c));  // open: dp
  _7_Segment_Display u_7_segment_display_4 (
    .g(binario_7_segmentos_1_g_2), .f(binario_7_segmentos_1_f_2), .a(binario_7_segmentos_1_a_2),
    .b(binario_7_segmentos_1_b_2), .e(binario_7_segmentos_1_e_2), .d(binario_7_segmentos_1_d_2),
    .c(binario_7_segmentos_1_c_2));  // open: dp
  _7_Segment_Display u_7_segment_display_5 (
    .g(binario_7_segmentos_1_g), .f(binario_7_segmentos_1_f), .a(binario_7_segmentos_1_a),
    .b(binario_7_segmentos_1_b), .e(binario_7_segmentos_1_e), .d(binario_7_segmentos_1_d),
    .c(binario_7_segmentos_1_c));  // open: dp
  \Binário___Gray  \binário_gray_1  (
    .Bit3(\decimal_binário_1_bit3 ), .Bit2(\decimal_binário_1_bit2 ), .Bit1(\decimal_binário_1_bit1 ),
    .Bit0(\decimal_binário_1_bit0 ), .bit3_2(\binário_gray_1_bit3_2 ), .bit2_2(\binário_gray_1_bit2_2 ),
    .bit1_2(\binário_gray_1_bit1_2 ), .bit0_2(\binário_gray_1_bit0_2 ));
  BINARIO___7_SEGMENTOS binario_7_segmentos_2 (
    .Bit3(\binário_gray_1_bit3_2 ), .Bit2(\binário_gray_1_bit2_2 ), .Bit1(\binário_gray_1_bit1_2 ),
    .Bit0(\binário_gray_1_bit0_2 ), .A(binario_7_segmentos_2_a), .B(binario_7_segmentos_2_b),
    .C(binario_7_segmentos_2_c), .D(binario_7_segmentos_2_d), .E(binario_7_segmentos_2_e),
    .F(binario_7_segmentos_2_f), .G(binario_7_segmentos_2_g), .A_2(binario_7_segmentos_2_a_2),
    .B_2(binario_7_segmentos_2_b_2), .C_2(binario_7_segmentos_2_c_2), .D_2(binario_7_segmentos_2_d_2),
    .E_2(binario_7_segmentos_2_e_2), .F_2(binario_7_segmentos_2_f_2), .G_2(binario_7_segmentos_2_g_2),
    .A_3(binario_7_segmentos_2_a_3), .B_3(binario_7_segmentos_2_b_3), .C_3(binario_7_segmentos_2_c_3),
    .D_3(binario_7_segmentos_2_d_3), .E_3(binario_7_segmentos_2_e_3), .F_3(binario_7_segmentos_2_f_3),
    .G_3(binario_7_segmentos_2_g_3), .A_4(binario_7_segmentos_2_a_4), .B_4(binario_7_segmentos_2_b_4),
    .C_4(binario_7_segmentos_2_c_4), .D_4(binario_7_segmentos_2_d_4), .E_4(binario_7_segmentos_2_e_4),
    .F_4(binario_7_segmentos_2_f_4), .G_4(binario_7_segmentos_2_g_4));
  _7_Segment_Display u_7_segment_display_6 (
    .g(binario_7_segmentos_2_g_3), .f(binario_7_segmentos_2_f_3), .a(binario_7_segmentos_2_a_3),
    .b(binario_7_segmentos_2_b_3), .e(binario_7_segmentos_2_e_3), .d(binario_7_segmentos_2_d_3),
    .c(binario_7_segmentos_2_c_3));  // open: dp
  _7_Segment_Display u_7_segment_display_7 (
    .g(binario_7_segmentos_2_g_4), .f(binario_7_segmentos_2_f_4), .a(binario_7_segmentos_2_a_4),
    .b(binario_7_segmentos_2_b_4), .e(binario_7_segmentos_2_e_4), .d(binario_7_segmentos_2_d_4),
    .c(binario_7_segmentos_2_c_4));  // open: dp
  _7_Segment_Display u_7_segment_display_8 (
    .g(binario_7_segmentos_2_g_2), .f(binario_7_segmentos_2_f_2), .a(binario_7_segmentos_2_a_2),
    .b(binario_7_segmentos_2_b_2), .e(binario_7_segmentos_2_e_2), .d(binario_7_segmentos_2_d_2),
    .c(binario_7_segmentos_2_c_2));  // open: dp
  _7_Segment_Display u_7_segment_display_9 (
    .g(binario_7_segmentos_2_g), .f(binario_7_segmentos_2_f), .a(binario_7_segmentos_2_a),
    .b(binario_7_segmentos_2_b), .e(binario_7_segmentos_2_e), .d(binario_7_segmentos_2_d),
    .c(binario_7_segmentos_2_c));  // open: dp

  // Notes on the sheet:
  //   DECIMAL
endmodule

module _7_segmentos (
  input  bit_3,
  input  bit_2,
  input  bit_1,
  input  bit_0,
  output A,
  output B,
  output C,
  output D,
  output E,
  output F,
  output G
);

  wire and_1_out, and_2_out, and_3_out, and_4_out, and_5_out, and_6_out, and_7_out, and_8_out, and_9_out,
       and_10_out;

  and and_1 (and_1_out, bit_2, bit_0);
  and and_2 (and_2_out, ~bit_2, ~bit_0);  // AND_Gate
  and and_3 (and_3_out, ~bit_1, ~bit_0);  // AND_Gate
  and and_4 (and_4_out, bit_1, bit_0);
  and and_5 (and_5_out, bit_1, ~bit_0);  // AND_Gate
  and and_6 (and_6_out, ~bit_2, bit_1);  // AND_Gate
  and and_7 (and_7_out, bit_2, ~bit_1, bit_0);  // AND_Gate
  and and_8 (and_8_out, bit_2, ~bit_1);  // AND_Gate
  and and_9 (and_9_out, bit_2, ~bit_0);  // AND_Gate
  and and_10 (and_10_out, ~bit_2, bit_1);  // AND_Gate
  or or_1 (A, bit_3, bit_1, and_1_out, and_2_out);
  or or_2 (B, ~bit_2, and_3_out, and_4_out);  // OR_Gate
  or or_3 (C, bit_2, ~bit_1, bit_0);  // OR_Gate
  or or_4 (D, bit_3, and_5_out, and_6_out, and_7_out, and_2_out);
  or or_5 (E, and_5_out, and_2_out);
  or or_6 (F, bit_3, and_3_out, and_8_out, and_9_out);
  or or_7 (G, bit_3, and_8_out, and_5_out, and_10_out);
  _7_Segment_Display u_7_segment_display_1 (.g(G), .f(F), .a(A), .b(B), .e(E), .d(D), .c(C));  // open: dp

  // Notes on the sheet:
  //   A
  //   C
  //   B
  //   D
endmodule

module \DECIMAL___BINÁRIO  (
  input  _0,
  input  _1,
  input  _2,
  input  _3,
  input  _4,
  input  _5,
  input  _6,
  input  _7,
  input  _8,
  input  _9,
  output bit3,
  output bit2,
  output bit1,
  output bit0
);

  or or_1 (bit3, _8, _9);
  or or_2 (bit2, _4, _5, _6, _7);
  or or_3 (bit1, _2, _3, _6, _7);
  or or_4 (bit0, _1, _3, _5, _7, _9);
endmodule

module \Binário___Gray  (
  input  Bit3,
  input  Bit2,
  input  Bit1,
  input  Bit0,
  output bit3_2,
  output bit2_2,
  output bit1_2,
  output bit0_2
);

  or or_1 (bit2_2, Bit3, Bit2);
  xor xor_1 (bit1_2, Bit2, Bit1);
  xor xor_2 (bit0_2, Bit1, Bit0);

  assign bit3_2 = Bit3;

  // Notes on the sheet:
  //   A
  //   D
  //   B
  //   C
endmodule

module BINARIO___7_SEGMENTOS (
  input  Bit3,
  input  Bit2,
  input  Bit1,
  input  Bit0,
  output A,
  output B,
  output C,
  output D,
  output E,
  output F,
  output G,
  output A_2,
  output B_2,
  output C_2,
  output D_2,
  output E_2,
  output F_2,
  output G_2,
  output A_3,
  output B_3,
  output C_3,
  output D_3,
  output E_3,
  output F_3,
  output G_3,
  output A_4,
  output B_4,
  output C_4,
  output D_4,
  output E_4,
  output F_4,
  output G_4
);

  _7_segmentos u_7_segmentos_1 (
    .bit_3(1'b0), .bit_2(1'b0), .bit_1(1'b0), .bit_0(Bit0), .A(A), .B(B), .C(C), .D(D), .E(E), .F(F), .G(G));
  _7_segmentos u_7_segmentos_2 (
    .bit_3(1'b0), .bit_2(1'b0), .bit_1(1'b0), .bit_0(Bit1), .A(A_2), .B(B_2), .C(C_2), .D(D_2), .E(E_2),
    .F(F_2), .G(G_2));
  _7_segmentos u_7_segmentos_3 (
    .bit_3(1'b0), .bit_2(1'b0), .bit_1(1'b0), .bit_0(Bit2), .A(A_3), .B(B_3), .C(C_3), .D(D_3), .E(E_3),
    .F(F_3), .G(G_3));
  _7_segmentos u_7_segmentos_4 (
    .bit_3(1'b0), .bit_2(1'b0), .bit_1(1'b0), .bit_0(Bit3), .A(A_4), .B(B_4), .C(C_4), .D(D_4), .E(E_4),
    .F(F_4), .G(G_4));
endmodule
