// Logisim project decimal - 7seg.circ as structural Verilog: 2 circuits, main circuit main
module main (
);

  wire _0_out, _1_out, _2_out, _3_out, _4_out, _5_out, _6_out, _7_out, _8_out, _9_out,
       decimal_7_segmentos_1_a, decimal_7_segmentos_1_b, decimal_7_segmentos_1_c, decimal_7_segmentos_1_d,
       decimal_7_segmentos_1_e, decimal_7_segmentos_1_f, decimal_7_segmentos_1_g;

  Button _0 (.out(_0_out));
  Button _1 (.out(_1_out));
  Button _4 (.out(_4_out));
  Button _2 (.out(_2_out));
  Button _3 (.out(_3_out));
  Button _6 (.out(_6_out));
  Button _5 (.out(_5_out));
  Decimal___7_segmentos decimal_7_segmentos_1 (
    ._0(_0_out), ._1(_1_out), ._2(_2_out), ._3(_3_out), ._4(_4_out), ._5(_5_out), ._6(_6_out), ._7(_7_out),
    ._8(_8_out), ._9(_9_out), .a(decimal_7_segmentos_1_a), .b(decimal_7_segmentos_1_b),
    .c(decimal_7_segmentos_1_c), .d(decimal_7_segmentos_1_d), .e(decimal_7_segmentos_1_e),
    .f(decimal_7_segmentos_1_f), .g(decimal_7_segmentos_1_g));
  Button _8 (.out(_8_out));
  Button _7 (.out(_7_out));
  Button _9 (.out(_9_out));
  _7_Segment_Display u_7_segment_display_1 (
    .g(decimal_7_segmentos_1_g), .f(decimal_7_segmentos_1_f), .a(decimal_7_segmentos_1_a),
    .b(decimal_7_segmentos_1_b), .e(decimal_7_segmentos_1_e), .d(decimal_7_segmentos_1_d),
    .c(decimal_7_segmentos_1_c));  // open: dp
endmodule

module Decimal___7_segmentos (
  input  _0,
  input  _1,
  input  _2,
  input  _3,
  input  _4,
  input  _5,
  input  _6,
  input  _7,
  input  _8,
  input  _9,
  output a,
  output b,
  output c,
  output d,
  output e,
  output f,
  output g
);

  or or_1 (a, _0, _2, _3, _5, _6, _7, _8, _9);
  or or_2 (b, _0, _1, _2, _3, _4, _7, _8, _9);
  or or_3 (c, _0, _1, _3, _4, _5, _6, _7, _8, _9);
  or or_4 (d, _0, _2, _3, _5, _6, _8, _9);
  or or_5 (e, _0, _2, _6, _8);
  or or_6 (f, _0, _4, _5, _6, _8, _9);
  or or_7 (g, _2, _3, _4, _5, _6, _8, _9);
endmodule
