// Logisim project decimal-binario-7seg.circ as structural Verilog: 4 circuits, main circuit main
module main (
);

  wire _0_out, _1_out, _2_out, _3_out, _4_out, _5_out, _6_out, _7_out, _8_out, _9_out,
       codificar_para_decimal_binario_1_bit_0, codificar_para_decimal_binario_1_bit_1,
       codificar_para_decimal_binario_1_bit_2, codificar_para_decimal_binario_1_bit_3,
       decodificar_binario_segmento_1_out_5, decodificar_binario_segmento_1_out_6,
       decodificar_binario_segmento_1_out_7, decodificar_binario_segmento_1_out_8,
       decodificar_binario_segmento_1_out_9, decodificar_binario_segmento_1_out_10,
       decodificar_binario_segmento_1_out_11;

  Button _9 (.out(_9_out));
  Button _8 (.out(_8_out));
  Button _7 (.out(_7_out));
  Button _6 (.out(_6_out));
  codificar_para_decimal_binario codificar_para_decimal_binario_1 (
    ._9(_9_out), ._8(_8_out), ._7(_7_out), ._6(_6_out), ._5(_5_out), ._4(_4_out), ._3(_3_out), ._2(_2_out),
    ._1(_1_out), ._0(_0_out), .Bit_3(codificar_para_decimal_binario_1_bit_3),
    .Bit_2(codificar_para_decimal_binario_1_bit_2), .Bit_1(codificar_para_decimal_binario_1_bit_1),
    .Bit_0(codificar_para_decimal_binario_1_bit_0));
  Button _5 (.out(_5_out));
  Button _4 (.out(_4_out));
  Button _3 (.out(_3_out));
  decodificar_binario_segmento decodificar_binario_segmento_1 (
    .bit_3(codificar_para_decimal_binario_1_bit_3), .bit_2(codificar_para_decimal_binario_1_bit_2),
    .bit_1(codificar_para_decimal_binario_1_bit_1), .bit_0(codificar_para_decimal_binario_1_bit_0),
    .out_5(decodificar_binario_segmento_1_out_5), .out_6(decodificar_binario_segmento_1_out_6),
    .out_7(decodificar_binario_segmento_1_out_7), .out_8(decodificar_binario_segmento_1_out_8),
    .out_9(decodificar_binario_segmento_1_out_9), .out_10(decodificar_binario_segmento_1_out_10),
    .out_11(decodificar_binario_segmento_1_out_11));
  Button _0 (.out(_0_out));
  Button _1 (.out(_1_out));
  Button _2 (.out(_2_out));
  _7_Segment_Display u_7_segment_display_1 (
    .g(decodificar_binario_segmento_1_out_11), .f(decodificar_binario_segmento_1_out_10),
    .a(decodificar_binario_segmento_1_out_5), .b(decodificar_binario_segmento_1_out_6),
    .e(decodificar_binario_segmento_1_out_9), .d(decodificar_binario_segmento_1_out_8),
    .c(decodificar_binario_segmento_1_out_7));  // open: dp
endmodule

module codificar_para_decimal_binario (
  input  _9,
  input  _8,
  input  _7,
  input  _6,
  input  _5,
  input  _4,
  input  _3,
  input  _2,
  input  _1,
  input  _0,
  output Bit_3,
  output Bit_2,
  output Bit_1,
  output Bit_0
);

  or or_1 (Bit_3, _8, _9);
  or or_2 (Bit_2, _4, _5, _6, _7);
  or or_3 (Bit_1, _2, _3, _6, _7);
  or or_4 (Bit_0, _1, _3, _5, _7, _9);
endmodule

module decodificar_binario_segmento (
  input  bit_3,
  input  bit_2,
  input  bit_1,
  input  bit_0,
  output out_5,
  output out_6,
  output out_7,
  output out_8,
  output out_9,
  output out_10,
  output out_11
);

  wire and_1_out, and_2_out, and_3_out, and_4_out, and_5_out, and_6_out, and_7_out, and_8_out, and_9_out,
       and_10_out, and_11_out, and_12_out, and_13_out, and_14_out, and_15_out;

  and and_1 (and_1_out, bit_2, bit_0);
  and and_2 (and_2_out, ~bit_1, ~bit_0);  // AND_Gate
  and and_3 (and_3_out, bit_1, bit_0);
  and and_4 (and_4_out, bit_1, ~bit_0);  // AND_Gate
  and and_5 (and_5_out, ~bit_2, bit_1);  // AND_Gate
  and and_6 (and_6_out, bit_2, ~bit_1, bit_0);  // AND_Gate
  and and_7 (and_7_out, ~bit_2, ~bit_0);  // AND_Gate
  and and_8 (and_8_out, bit_1, ~bit_0);  // AND_Gate
  and and_9 (and_9_out, ~bit_1, ~bit_0);  // AND_Gate
  and and_10 (and_10_out, bit_2, ~bit_1);  // AND_Gate
  and and_11 (and_11_out, bit_2, ~bit_0);  // AND_Gate
  and and_12 (and_12_out, ~bit_2, bit_1);  // AND_Gate
  and and_13 (and_13_out, bit_1, ~bit_0);  // AND_Gate
  and and_14 (and_14_out, bit_2, ~bit_1);  // AND_Gate
  and and_15 (and_15_out, ~bit_2, ~bit_0);  // AND_Gate
  or A (out_5, bit_3, bit_1, and_1_out, and_15_out);
  or B (out_6, ~bit_2, and_2_out, and_3_out);  // OR_Gate
  or C (out_7, bit_2, ~bit_1, bit_0);  // OR_Gate
  or D (out_8, bit_3, and_4_out, and_5_out, and_6_out, and_15_out);
  or E (out_9, and_7_out, and_8_out);
  or F (out_10, bit_3, and_9_out, and_10_out, and_11_out);
  or G (out_11, and_12_out, bit_3, and_13_out, and_14_out);

  // Notes on the sheet:
  //   A
  //   B
  //   D
  //   C
endmodule

module segmento (
  input  B,
  input  A,
  input  F,
  input  G,
  input  E,
  input  D,
  input  C
);

  _7_Segment_Display u_7_segment_display_1 (.g(G), .f(F), .a(A), .b(B), .e(E), .d(D), .c(C));  // open: dp
endmodule
