// Logisim project relogio.circ as structural Verilog: 7 circuits, main circuit main
module main (
);

  wire binario_7seg_1_a, binario_7seg_1_b, binario_7seg_1_c, binario_7seg_1_d, binario_7seg_1_e,
       binario_7seg_1_f, binario_7seg_1_g, binario_7seg_2_a, binario_7seg_2_b, binario_7seg_2_c,
       binario_7seg_2_d, binario_7seg_2_e, binario_7seg_2_f, binario_7seg_2_g, binario_7seg_3_a,
       binario_7seg_3_b, binario_7seg_3_c, binario_7seg_3_d, binario_7seg_3_e, binario_7seg_3_f,
       binario_7seg_3_g, binario_7seg_4_a, binario_7seg_4_b, binario_7seg_4_c, binario_7seg_4_d,
       binario_7seg_4_e, binario_7seg_4_f, binario_7seg_4_g, binario_7seg_5_a, binario_7seg_5_b,
       binario_7seg_5_c, binario_7seg_5_d, binario_7seg_5_e, binario_7seg_5_f, binario_7seg_5_g, clock_1_out,
       contador_0_2_1_bit0, contador_0_2_1_bit1, contador_0_2_1_out_2, contador_0_5_1_bit0,
       contador_0_5_1_bit1, contador_0_5_1_bit3, contador_0_5_1_out_3, contador_0_5_2_bit0,
       contador_0_5_2_bit1, contador_0_5_2_bit3, contador_0_5_2_out_3, contador_0_9_1_bit0,
       contador_0_9_1_bit1, contador_0_9_1_bit2, contador_0_9_1_bit3, contador_0_9_1_clock_saida,
       contador_0_9_2_bit0, contador_0_9_2_bit1, contador_0_9_2_bit2, contador_0_9_2_bit3,
       contador_0_9_2_clock_saida, contador_0_9_aux_1_bit0, contador_0_9_aux_1_bit1, contador_0_9_aux_1_bit2,
       contador_0_9_aux_1_bit3, contador_0_9_aux_1_clock_saida, contador_0_9_aux_1_out_3, n1_e_2_7_seg_1_a,
       n1_e_2_7_seg_1_b, n1_e_2_7_seg_1_c, n1_e_2_7_seg_1_d, n1_e_2_7_seg_1_e, n1_e_2_7_seg_1_f,
       n1_e_2_7_seg_1_g, not_1_out;

  contador_0_2 contador_0_2_1 (
    .out_2(contador_0_2_1_out_2), .clock(contador_0_9_aux_1_clock_saida), .bit0(contador_0_2_1_bit0),
    .bit1(contador_0_2_1_bit1));
  _1_e_2_7_seg u_1_e_2_7_seg_1 (
    .bit1(contador_0_2_1_bit1), .bit0(contador_0_2_1_bit0), .a(n1_e_2_7_seg_1_a), .b(n1_e_2_7_seg_1_b),
    .c(n1_e_2_7_seg_1_c), .d(n1_e_2_7_seg_1_d), .e(n1_e_2_7_seg_1_e), .f(n1_e_2_7_seg_1_f),
    .g(n1_e_2_7_seg_1_g));
  _7_Segment_Display u_7_segment_display_1 (
    .g(n1_e_2_7_seg_1_a), .f(n1_e_2_7_seg_1_b), .a(n1_e_2_7_seg_1_c), .b(n1_e_2_7_seg_1_d),
    .e(n1_e_2_7_seg_1_g), .d(n1_e_2_7_seg_1_f), .c(n1_e_2_7_seg_1_e));  // open: dp
  contador_0_9_aux contador_0_9_aux_1 (
    .in_1(contador_0_2_1_out_2), .Clock_Saida(contador_0_9_aux_1_clock_saida), .CLOCK(contador_0_5_1_out_3),
    .out_3(contador_0_9_aux_1_out_3), .BIT0(contador_0_9_aux_1_bit0), .bit1(contador_0_9_aux_1_bit1),
    .bit2(contador_0_9_aux_1_bit2), .bit3(contador_0_9_aux_1_bit3));
  not not_1 (not_1_out, contador_0_9_aux_1_out_3);
  binario_7seg binario_7seg_1 (
    .bit3(contador_0_9_aux_1_bit3), .bit2(contador_0_9_aux_1_bit2), .bit1(contador_0_9_aux_1_bit1),
    .bit0(contador_0_9_aux_1_bit0), .a(binario_7seg_1_a), .b(binario_7seg_1_b), .c(binario_7seg_1_c),
    .d(binario_7seg_1_d), .e(binario_7seg_1_e), .f(binario_7seg_1_f), .g(binario_7seg_1_g));
  _7_Segment_Display u_7_segment_display_2 (
    .g(binario_7seg_1_a), .f(binario_7seg_1_b), .a(binario_7seg_1_c), .b(binario_7seg_1_d),
    .e(binario_7seg_1_g), .d(binario_7seg_1_f), .c(binario_7seg_1_e));  // open: dp
  contador_0_5 contador_0_5_1 (
    .in_1(not_1_out), .out_3(contador_0_5_1_out_3), .clock(contador_0_9_1_clock_saida),
    .bit0(contador_0_5_1_bit0), .bit1(contador_0_5_1_bit1), .bit3(contador_0_5_1_bit3));
  Button button_1 ();  // open: out
  Button button_2 ();  // open: out
  contador_0_9 contador_0_9_1 (
    .in_1(not_1_out), .Clock_Saida(contador_0_9_1_clock_saida), .CLOCK(contador_0_5_2_out_3),
    .BIT0(contador_0_9_1_bit0), .bit1(contador_0_9_1_bit1), .bit2(contador_0_9_1_bit2),
    .bit3(contador_0_9_1_bit3));
  binario_7seg binario_7seg_2 (
    .bit3(1'b0), .bit2(contador_0_5_1_bit3), .bit1(contador_0_5_1_bit1), .bit0(contador_0_5_1_bit0),
    .a(binario_7seg_2_a), .b(binario_7seg_2_b), .c(binario_7seg_2_c), .d(binario_7seg_2_d),
    .e(binario_7seg_2_e), .f(binario_7seg_2_f), .g(binario_7seg_2_g));
  _7_Segment_Display u_7_segment_display_3 (
    .g(binario_7seg_2_a), .f(binario_7seg_2_b), .a(binario_7seg_2_c), .b(binario_7seg_2_d),
    .e(binario_7seg_2_g), .d(binario_7seg_2_f), .c(binario_7seg_2_e));  // open: dp
  binario_7seg binario_7seg_3 (
    .bit3(contador_0_9_1_bit3), .bit2(contador_0_9_1_bit2), .bit1(contador_0_9_1_bit1),
    .bit0(contador_0_9_1_bit0), .a(binario_7seg_3_a), .b(binario_7seg_3_b), .c(binario_7seg_3_c),
    .d(binario_7seg_3_d), .e(binario_7seg_3_e), .f(binario_7seg_3_f), .g(binario_7seg_3_g));
  contador_0_5 contador_0_5_2 (
    .in_1(not_1_out), .out_3(contador_0_5_2_out_3), .clock(contador_0_9_2_clock_saida),
    .bit0(contador_0_5_2_bit0), .bit1(contador_0_5_2_bit1), .bit3(contador_0_5_2_bit3));
  _7_Segment_Display u_7_segment_display_4 (
    .g(binario_7seg_3_a), .f(binario_7seg_3_b), .a(binario_7seg_3_c), .b(binario_7seg_3_d),
    .e(binario_7seg_3_g), .d(binario_7seg_3_f), .c(binario_7seg_3_e));  // open: dp
  Clock clock_1 (.out(clock_1_out));
  binario_7seg binario_7seg_4 (
    .bit3(1'b0), .bit2(contador_0_5_2_bit3), .bit1(contador_0_5_2_bit1), .bit0(contador_0_5_2_bit0),
    .a(binario_7seg_4_a), .b(binario_7seg_4_b), .c(binario_7seg_4_c), .d(binario_7seg_4_d),
    .e(binario_7seg_4_e), .f(binario_7seg_4_f), .g(binario_7seg_4_g));
  _7_Segment_Display u_7_segment_display_5 (
    .g(binario_7seg_4_a), .f(binario_7seg_4_b), .a(binario_7seg_4_c), .b(binario_7seg_4_d),
    .e(binario_7seg_4_g), .d(binario_7seg_4_f), .c(binario_7seg_4_e));  // open: dp
  Button button_3 ();  // open: out
  Button button_4 ();  // open: out
  contador_0_9 contador_0_9_2 (
    .in_1(not_1_out), .Clock_Saida(contador_0_9_2_clock_saida), .CLOCK(clock_1_out),
    .BIT0(contador_0_9_2_bit0), .bit1(contador_0_9_2_bit1), .bit2(contador_0_9_2_bit2),
    .bit3(contador_0_9_2_bit3));
  binario_7seg binario_7seg_5 (
    .bit3(contador_0_9_2_bit3), .bit2(contador_0_9_2_bit2), .bit1(contador_0_9_2_bit1),
    .bit0(contador_0_9_2_bit0), .a(binario_7seg_5_a), .b(binario_7seg_5_b), .c(binario_7seg_5_c),
    .d(binario_7seg_5_d), .e(binario_7seg_5_e), .f(binario_7seg_5_f), .g(binario_7seg_5_g));
  _7_Segment_Display u_7_segment_display_6 (
    .g(binario_7seg_5_a), .f(binario_7seg_5_b), .a(binario_7seg_5_c), .b(binario_7seg_5_d),
    .e(binario_7seg_5_g), .d(binario_7seg_5_f), .c(binario_7seg_5_e));  // open: dp
endmodule

module binario_7seg (
  input  bit3,
  input  bit2,
  input  bit1,
  input  bit0,
  output a,
  output b,
  output c,
  output d,
  output e,
  output f,
  output g
);

  wire and_1_out, and_2_out, and_3_out, and_4_out, and_5_out, and_6_out, and_7_out, and_8_out, and_9_out,
       and_10_out, and_11_out, and_12_out, and_13_out, and_14_out, and_15_out, and_16_out, not_1_out,
       not_2_out, not_3_out, not_4_out, not_5_out, not_6_out, not_7_out, not_8_out, not_9_out, not_10_out,
       not_11_out, not_12_out, not_13_out, not_14_out, not_15_out, not_16_out, not_17_out, not_18_out,
       not_19_out, not_20_out, not_21_out;

  not not_1 (not_1_out, bit2);
  and and_1 (and_1_out, not_1_out, bit1);
  and and_2 (and_2_out, bit2, not_2_out);
  not not_2 (not_2_out, bit1);
  and and_3 (and_3_out, bit2, not_3_out);
  not not_3 (not_3_out, bit0);
  not not_4 (not_4_out, bit1);
  and and_4 (and_4_out, not_4_out, not_5_out);
  not not_5 (not_5_out, bit0);
  and and_5 (and_5_out, bit2, not_6_out);
  not not_6 (not_6_out, bit1);
  and and_6 (and_6_out, bit2, not_7_out);
  not not_7 (not_7_out, bit0);
  not not_8 (not_8_out, bit2);
  and and_7 (and_7_out, not_8_out, not_9_out);
  not not_9 (not_9_out, bit0);
  and and_8 (and_8_out, bit2, bit0);
  not not_10 (not_10_out, bit2);
  not not_11 (not_11_out, bit1);
  and and_9 (and_9_out, not_11_out, not_12_out);
  not not_12 (not_12_out, bit0);
  and and_10 (and_10_out, bit1, bit0);
  not not_13 (not_13_out, bit1);
  or or_1 (e, not_13_out, bit0, bit2);
  not not_14 (not_14_out, bit2);
  and and_11 (and_11_out, not_14_out, not_15_out);
  not not_15 (not_15_out, bit0);
  not not_16 (not_16_out, bit2);
  and and_12 (and_12_out, not_16_out, bit1);
  and and_13 (and_13_out, bit1, not_17_out);
  not not_17 (not_17_out, bit0);
  and and_14 (and_14_out, bit2, not_18_out, bit0);
  not not_18 (not_18_out, bit1);
  not not_19 (not_19_out, bit2);
  and and_15 (and_15_out, not_19_out, not_20_out);
  not not_20 (not_20_out, bit0);
  and and_16 (and_16_out, bit1, not_21_out);
  not not_21 (not_21_out, bit0);
  or or_2 (a, and_1_out, and_2_out, and_3_out, bit3);
  or or_3 (b, and_4_out, and_5_out, and_6_out, bit3);
  or or_4 (c, and_7_out, bit1, and_8_out, bit3);
  or or_5 (d, not_10_out, and_9_out, and_10_out);
  or or_6 (f, and_11_out, and_12_out, and_13_out, and_14_out, bit3);
  or or_7 (g, and_15_out, and_16_out);
endmodule

module contador_0_9 (
  input  in_1,
  input  CLOCK,
  output Clock_Saida,
  output BIT0,
  output bit1,
  output bit2,
  output bit3
);

  wire j_k_ff_1_qn, j_k_ff_2_qn, j_k_ff_3_qn;

  and and_1 (Clock_Saida, bit3, bit1);
  J_K_Flip_Flop j_k_ff_1 (
    .J(1'b1), .clk(CLOCK), .K(1'b1), .Q(BIT0), .Qn(j_k_ff_1_qn), .en(in_1), .reset(Clock_Saida));  // open: preset
  J_K_Flip_Flop j_k_ff_2 (
    .J(1'b1), .clk(j_k_ff_1_qn), .K(1'b1), .Q(bit1), .Qn(j_k_ff_2_qn), .en(in_1), .reset(Clock_Saida));  // open: preset
  J_K_Flip_Flop j_k_ff_3 (
    .J(1'b1), .clk(j_k_ff_2_qn), .K(1'b1), .Q(bit2), .Qn(j_k_ff_3_qn), .en(in_1), .reset(Clock_Saida));  // open: preset
  J_K_Flip_Flop j_k_ff_4 (
    .J(1'b1), .clk(j_k_ff_3_qn), .K(1'b1), .Q(bit3), .en(in_1), .reset(Clock_Saida));  // open: Qn, preset
endmodule

module contador_0_5 (
  input  in_1,
  input  clock,
  output out_3,
  output bit0,
  output bit1,
  output bit3
);

  wire j_k_ff_1_qn, j_k_ff_2_qn;

  and and_1 (out_3, bit3, bit1);
  J_K_Flip_Flop j_k_ff_1 (
    .J(1'b1), .clk(clock), .K(1'b1), .Q(bit0), .Qn(j_k_ff_1_qn), .en(in_1), .reset(out_3));  // open: preset
  J_K_Flip_Flop j_k_ff_2 (
    .J(1'b1), .clk(j_k_ff_1_qn), .K(1'b1), .Q(bit1), .Qn(j_k_ff_2_qn), .en(in_1), .reset(out_3));  // open: preset
  J_K_Flip_Flop j_k_ff_3 (
    .J(1'b1), .clk(j_k_ff_2_qn), .K(1'b1), .Q(bit3), .en(in_1), .reset(out_3));  // open: Qn, preset
endmodule

module _1_e_2_7_seg (
  input  bit1,
  input  bit0,
  output a,
  output b,
  output c,
  output d,
  output e,
  output f,
  output g
);

  wire not_1_out, not_2_out;

  not not_1 (not_1_out, bit1);
  not not_2 (not_2_out, bit0);
  not not_3 (c, bit0);
  not not_4 (e, bit1);
  not not_5 (f, bit0);
  not not_6 (g, bit0);
  and and_1 (b, not_1_out, not_2_out);

  assign a = bit1;
  assign d = 1'b1;
endmodule

module contador_0_2 (
  input  clock,
  output out_2,
  output bit0,
  output bit1
);

  wire j_k_ff_1_qn;

  J_K_Flip_Flop j_k_ff_1 (.J(1'b1), .clk(clock), .K(1'b1), .Q(bit0), .Qn(j_k_ff_1_qn));  // open: preset, en, reset
  J_K_Flip_Flop j_k_ff_2 (.J(1'b1), .clk(j_k_ff_1_qn), .K(1'b1), .Q(bit1));  // open: Qn, preset, en, reset

  assign out_2 = bit1;
endmodule

module contador_0_9_aux (
  input  in_1,
  input  CLOCK,
  output out_3,
  output Clock_Saida,
  output BIT0,
  output bit1,
  output bit2,
  output bit3
);

  wire j_k_ff_1_qn, j_k_ff_2_qn, j_k_ff_3_qn;

  and and_1 (out_3, in_1, bit2);
  and and_2 (Clock_Saida, bit3, bit1);
  J_K_Flip_Flop j_k_ff_1 (
    .J(1'b1), .clk(CLOCK), .K(1'b1), .Q(BIT0), .Qn(j_k_ff_1_qn), .reset(Clock_Saida));  // open: preset, en
  J_K_Flip_Flop j_k_ff_2 (
    .J(1'b1), .clk(j_k_ff_1_qn), .K(1'b1), .Q(bit1), .Qn(j_k_ff_2_qn), .reset(Clock_Saida));  // open: preset, en
  J_K_Flip_Flop j_k_ff_3 (
    .J(1'b1), .clk(j_k_ff_2_qn), .K(1'b1), .Q(bit2), .Qn(j_k_ff_3_qn), .reset(Clock_Saida));  // open: preset, en
  J_K_Flip_Flop j_k_ff_4 (
    .J(1'b1), .clk(j_k_ff_3_qn), .K(1'b1), .Q(bit3), .reset(Clock_Saida));  // open: Qn, preset, en
endmodule
